// Logisim project ALU_Logisim.circ as structural Verilog: 8 circuits, main circuit main
module main (
  input  [8:0] in_1,
  input  [8:0] in_2,
  input  [2:0] in_3,
  output Carry_flag,
  output [8:0] Result,
  output Zero_flag
);

  ALU_Top alu_top_1 (.A(in_1), .B(in_2), .Alu_Control(in_3), .out_4(Carry_flag), .result(Result), .out_6(Zero_flag));
endmodule

module FullAdder (
  input  A,
  input  B,
  input  Cin,
  output Cout,
  output sum
);

  wire and_1_out, and_2_out, xor_1_out;

  xor xor_1 (xor_1_out, A, B);
  and and_1 (and_1_out, A, B);
  and and_2 (and_2_out, Cin, xor_1_out);
  or or_1 (Cout, and_1_out, and_2_out);
  xor xor_2 (sum, xor_1_out, Cin);

  // Notes on the sheet:
  //   A
  //   B
  //   Cin
  //   Cout
  //   Sum
endmodule

module ALU_Add (
  input  [8:0] A,
  input  [8:0] B,
  output [8:0] sum_out
);

  wire fulladder_1_cout, fulladder_2_cout, fulladder_3_cout, fulladder_4_cout, fulladder_5_cout,
       fulladder_6_cout, fulladder_7_cout, fulladder_8_cout;

  FullAdder fulladder_1 (.A(A[0]), .B(B[0]), .Cin(1'b0), .Cout(fulladder_1_cout), .sum(sum_out[0]));
  FullAdder fulladder_2 (.A(A[1]), .B(B[1]), .Cin(fulladder_1_cout), .Cout(fulladder_2_cout), .sum(sum_out[1]));
  FullAdder fulladder_3 (.A(A[2]), .B(B[2]), .Cin(fulladder_2_cout), .Cout(fulladder_3_cout), .sum(sum_out[2]));
  FullAdder fulladder_4 (.A(A[3]), .B(B[3]), .Cin(fulladder_3_cout), .Cout(fulladder_4_cout), .sum(sum_out[3]));
  FullAdder fulladder_5 (.A(A[4]), .B(B[4]), .Cin(fulladder_4_cout), .Cout(fulladder_5_cout), .sum(sum_out[4]));
  FullAdder fulladder_6 (.A(A[5]), .B(B[5]), .Cin(fulladder_5_cout), .Cout(fulladder_6_cout), .sum(sum_out[5]));
  FullAdder fulladder_7 (.A(A[6]), .B(B[6]), .Cin(fulladder_6_cout), .Cout(fulladder_7_cout), .sum(sum_out[6]));
  FullAdder fulladder_8 (.A(A[7]), .B(B[7]), .Cin(fulladder_7_cout), .Cout(fulladder_8_cout), .sum(sum_out[7]));
  FullAdder fulladder_9 (.A(A[8]), .B(B[8]), .Cin(fulladder_8_cout), .sum(sum_out[8]));  // open: Cout

  // Notes on the sheet:
  //   sum_out: pull=up
endmodule

module ALU_Sub (
  input  [8:0] A,
  input  [8:0] B,
  output [8:0] sum_out
);

  wire fulladder_1_cout, fulladder_2_cout, fulladder_3_cout, fulladder_4_cout, fulladder_5_cout,
       fulladder_6_cout, fulladder_7_cout, fulladder_8_cout;
  wire [8:0] not_1_out;

  assign not_1_out = ~B;  // NOT_Gate not_1, 9 bits wide
  FullAdder fulladder_1 (.A(A[0]), .B(not_1_out[0]), .Cin(1'b0), .Cout(fulladder_1_cout), .sum(sum_out[0]));
  FullAdder fulladder_2 (.A(A[1]), .B(not_1_out[1]), .Cin(fulladder_1_cout), .Cout(fulladder_2_cout), .sum(sum_out[1]));
  FullAdder fulladder_3 (.A(A[2]), .B(not_1_out[2]), .Cin(fulladder_2_cout), .Cout(fulladder_3_cout), .sum(sum_out[2]));
  FullAdder fulladder_4 (.A(A[3]), .B(not_1_out[3]), .Cin(fulladder_3_cout), .Cout(fulladder_4_cout), .sum(sum_out[3]));
  FullAdder fulladder_5 (.A(A[4]), .B(not_1_out[4]), .Cin(fulladder_4_cout), .Cout(fulladder_5_cout), .sum(sum_out[4]));
  FullAdder fulladder_6 (.A(A[5]), .B(not_1_out[5]), .Cin(fulladder_5_cout), .Cout(fulladder_6_cout), .sum(sum_out[5]));
  FullAdder fulladder_7 (.A(A[6]), .B(not_1_out[6]), .Cin(fulladder_6_cout), .Cout(fulladder_7_cout), .sum(sum_out[6]));
  FullAdder fulladder_8 (.A(A[7]), .B(not_1_out[7]), .Cin(fulladder_7_cout), .Cout(fulladder_8_cout), .sum(sum_out[7]));
  FullAdder fulladder_9 (.A(A[8]), .B(not_1_out[8]), .Cin(fulladder_8_cout), .sum(sum_out[8]));  // open: Cout

  // Notes on the sheet:
  //   sum_out: pull=up
endmodule

module ALU_Logic (
  input  [8:0] A,
  input  [8:0] B,
  output [8:0] And_out,
  output [8:0] Or_out
);

  assign And_out = A & B;  // AND_Gate and_1, 9 bits wide
  assign Or_out = A | B;  // OR_Gate or_1, 9 bits wide
endmodule

module ALU_ShiftL (
  input  [8:0] A,
  output [8:0] sll_out
);


  assign sll_out = {A[7:0], 1'b0};
endmodule

module ALU_ShiftR (
  input  [8:0] A,
  output [8:0] slr_out
);


  assign slr_out = {A[7:0], 1'b0};
endmodule

module ALU_Top (
  input  [8:0] A,
  input  [8:0] B,
  input  [2:0] Alu_Control,
  output out_4,
  output [8:0] result,
  output out_6
);

  wire [8:0] alu_add_1_sum_out, alu_logic_1_and_out, alu_logic_1_or_out, alu_shiftl_1_sll_out,
       alu_shiftr_1_slr_out, alu_sub_1_sum_out;

  ALU_Add alu_add_1 (.A(A), .B(B), .sum_out(alu_add_1_sum_out));
  ALU_Logic alu_logic_1 (.A(A), .B(B), .And_out(alu_logic_1_and_out), .Or_out(alu_logic_1_or_out));
  ALU_Sub alu_sub_1 (.A(A), .B(B), .sum_out(alu_sub_1_sum_out));
  ALU_ShiftL alu_shiftl_1 (.A(A), .sll_out(alu_shiftl_1_sll_out));
  ALU_ShiftR alu_shiftr_1 (.A(A), .slr_out(alu_shiftr_1_slr_out));
  Multiplexer #(.select(3), .width(9)) multiplexer_1 (
    .in0(alu_logic_1_and_out), .in1(alu_logic_1_or_out), .in2(alu_add_1_sum_out), .in3(alu_sub_1_sum_out),
    .in4(alu_shiftl_1_sll_out), .in5(alu_shiftr_1_slr_out), .in6({9{1'b0}}), .out(result), .sel(Alu_Control));  // open: in7
  Comparator #(.width(9)) comparator_1 (.a(result), .b({9{1'b0}}), .eq(out_6));  // open: gt, lt

  assign out_4 = 1'b0;
endmodule
