// Logisim project CLa2.circ as structural Verilog: 3 circuits, main circuit main
module main (
);

  CLA cla_1 ();  // open: A, B, Cin, S, Cout
endmodule

module CLA (
  input  A,
  input  B,
  input  Cin,
  output S,
  output Cout
);

  wire and_2_out, and_3_out, not_1_out, not_2_out;

  not not_1 (not_1_out, B);
  not not_2 (not_2_out, Cin);
  and and_1 (S, A, not_1_out, not_2_out);
  and and_2 (and_2_out, A, B);
  and and_3 (and_3_out, A, not_1_out, Cin);
  or or_1 (Cout, and_2_out, and_3_out);
endmodule

module CLA2 (
  input  C0,
  input  A0,
  input  B0,
  input  A1,
  input  B1,
  input  A2,
  input  d2,
  input  A3,
  input  d3,
  output S0,
  output S1,
  output S2,
  output S3,
  output C4
);

  wire adder_1_cout, adder_2_cout, adder_3_cout;

  Adder #(.width(1)) adder_1 (.a(A0), .b(B0), .out(S0), .cin(C0), .cout(adder_1_cout));
  Adder #(.width(1)) adder_2 (.a(A1), .b(B1), .out(S1), .cin(adder_1_cout), .cout(adder_2_cout));
  Adder #(.width(1)) adder_3 (.a(A2), .b(d2), .out(S2), .cin(adder_2_cout), .cout(adder_3_cout));
  Adder #(.width(1)) adder_4 (.a(A3), .b(d3), .out(S3), .cin(adder_3_cout), .cout(C4));
endmodule
