// Logisim project PreffixAder3.circ as structural Verilog
module PreffixAdder3 (
  input  A,
  input  B,
  input  Cin,
  output S,
  output Cout
);

  wire and_2_out, and_3_out, not_1_out, not_2_out;

  not not_1 (not_1_out, B);
  not not_2 (not_2_out, Cin);
  and and_1 (S, A, not_1_out, not_2_out);
  and and_2 (and_2_out, A, B);
  and and_3 (and_3_out, A, not_1_out, Cin);
  or or_1 (Cout, and_2_out, and_3_out);
endmodule

module PA3 (
  input  A,
  input  B,
  input  Cin,
  output S,
  output Cout
);

  wire and_2_out, and_3_out, not_1_out, not_2_out;

  not not_1 (not_1_out, B);
  not not_2 (not_2_out, Cin);
  and and_1 (S, A, not_1_out, not_2_out);
  and and_2 (and_2_out, A, B);
  and and_3 (and_3_out, A, not_1_out, Cin);
  or or_1 (Cout, and_2_out, and_3_out);
endmodule
