// Logisim project Sumadores.circ as structural Verilog
module CLA (
  input  A,
  input  B,
  input  Cin,
  output S,
  output Cout
);

  wire and_2_out, and_3_out, not_1_out, not_2_out;

  not not_1 (not_1_out, B);
  not not_2 (not_2_out, Cin);
  and and_1 (S, A, not_1_out, not_2_out);
  and and_2 (and_2_out, A, B);
  and and_3 (and_3_out, A, not_1_out, Cin);
  or or_1 (Cout, and_2_out, and_3_out);
endmodule

module RippleCarry (
  input  [3:0] A,
  input  [3:0] B,
  output [3:0] Sum
);

  wire cla_1_cout, cla_2_cout, cla_3_cout;

  CLA cla_1 (.A(A[0]), .B(B[0]), .Cin(1'b0), .S(Sum[0]), .Cout(cla_1_cout));
  CLA cla_2 (.A(A[1]), .B(B[1]), .Cin(cla_1_cout), .S(Sum[1]), .Cout(cla_2_cout));
  CLA cla_3 (.A(A[2]), .B(B[2]), .Cin(cla_2_cout), .S(Sum[2]), .Cout(cla_3_cout));
  CLA cla_4 (.A(A[3]), .B(B[3]), .Cin(cla_3_cout), .S(Sum[3]));  // open: Cout
endmodule

module PreffixAdder (
  input  [3:0] A,
  input  [3:0] B,
  input  Cin,
  output [3:0] Sum,
  output Cout
);

  wire and_1_out, and_2_out, and_3_out, and_4_out, prefixcell_1_g, prefixcell_1_p, prefixcell_2_g,
       prefixcell_2_p, prefixcell_3_p, xor_1_out, xor_2_out, xor_3_out, xor_4_out;

  xor xor_1 (xor_1_out, A[0], B[3]);
  xor xor_2 (xor_2_out, A[1], B[2]);
  xor xor_3 (xor_3_out, A[2], B[1]);
  xor xor_4 (xor_4_out, A[3], B[0]);
  and and_1 (and_1_out, A[0], B[0]);
  and and_2 (and_2_out, A[1], B[0]);
  and and_3 (and_3_out, A[2], B[2]);
  and and_4 (and_4_out, A[3], B[3]);
  Prefixcell prefixcell_1 (
    .Pi(xor_1_out), .Pj(xor_2_out), .Gi(and_1_out), .Gj(and_2_out), .P(prefixcell_1_p), .G(prefixcell_1_g));
  Prefixcell prefixcell_2 (
    .Pi(xor_3_out), .Pj(xor_4_out), .Gi(and_3_out), .Gj(and_4_out), .P(prefixcell_2_p), .G(prefixcell_2_g));
  Prefixcell prefixcell_3 (
    .Pi(prefixcell_1_p), .Pj(prefixcell_2_p), .Gi(prefixcell_1_g), .Gj(prefixcell_2_g), .P(prefixcell_3_p),
    .G(Cout));
  xor xor_5 (Sum[0], xor_1_out, and_1_out);
  xor xor_6 (Sum[1], prefixcell_1_p, Cin);
  xor xor_7 (Sum[2], prefixcell_2_p, prefixcell_1_g);
  xor xor_8 (Sum[3], prefixcell_3_p, prefixcell_2_g);

  // Notes on the sheet:
  //   P0
  //   P1
  //   P2
  //   P3
  //   G0
  //   G1
  //   G2
  //   G3
endmodule

module Prefixcell (
  input  Pi,
  input  Pj,
  input  Gi,
  input  Gj,
  output P,
  output G
);

  wire or_1_out;

  or or_1 (or_1_out, Gi, Gj);
  and and_1 (P, Pi, Pj);
  and and_2 (G, Pj, or_1_out);
endmodule
